# Fritzing sketch diagram (saved by Fritzing 0.8.7b)
breadboards: 1

parts:
  Part1 = Arduino Uno (Rev3)
  S1 = Pushbutton [package="[THT]"]
  R1 = Resistor [tolerance=±5% resistance=220 package=THT]
  LED1 = LED - 5mm [color="Red (633nm)" package="5 mm [THT]"]

nets:
  N1: Part1.D2, LED1.cathode
  N2: Part1.GND, S1.Pin_3, S1.Pin_4, R1.Pin_1
  N3: S1.Pin_1, S1.Pin_2
  N4: R1.Pin_0, LED1.anode
